// Logisim project IT012_Lab01_25522054.circ as structural Verilog: 6 circuits, main circuit Warmup
module Warmup (
  input  A,
  input  B,
  output x
);

  wire not_1_out;

  not not_1 (not_1_out, B);
  and and_1 (x, A, not_1_out);
endmodule

module TN1 (
  input  A,
  input  B,
  input  C,
  output A_prime,
  output AND,
  output OR,
  output NAND,
  output CHAIN,
  output NOR,
  output XOR,
  output NXOR,
  output XOR3,
  output NAND3
);

  not not_1 (A_prime, A);
  and and_1 (AND, A, B);
  or or_1 (OR, A, B);
  nand nand_1 (NAND, A, B);
  nor nor_1 (NOR, A, B);
  xor xor_1 (XOR, A, B);
  xnor xnor_1 (NXOR, A, B);
  xor xor_2 (XOR3, A, B, C);
  nand nand_2 (NAND3, A, B, C);
  nand nand_3 (CHAIN, NAND, C);
endmodule

module TN2 (
  input  in_1,
  input  in_2,
  input  in_3,
  output out_4,
  output out_5,
  output out_6,
  output out_7,
  output out_8
);

  wire and_1_out, and_2_out, and_3_out, and_4_out, and_5_out, not_1_out, not_2_out, not_3_out, not_4_out,
       not_5_out, or_1_out, or_2_out, or_3_out, or_4_out, or_5_out, or_6_out;

  not not_1 (not_1_out, in_1);
  not not_2 (not_2_out, in_1);
  not not_3 (not_3_out, in_2);
  or or_1 (or_1_out, in_1, in_2);
  buf and_1 (and_1_out, in_1);  // AND_Gate
  and and_2 (and_2_out, in_2, in_3);
  and and_3 (and_3_out, not_1_out, in_2);
  and and_4 (and_4_out, not_2_out, not_3_out);
  or or_2 (or_2_out, in_1, in_2);
  or or_3 (or_3_out, in_1, in_3);
  or or_4 (or_4_out, in_1, in_2);
  not not_4 (not_4_out, or_1_out);
  not not_5 (not_5_out, and_1_out);
  or or_5 (or_5_out, in_1, and_2_out);
  or or_6 (or_6_out, in_1, and_3_out);
  and and_5 (and_5_out, or_2_out, or_3_out);
  xnor xnor_1 (out_4, not_4_out, and_4_out);
  xnor xnor_2 (out_5, not_5_out, and_4_out);
  xnor xnor_3 (out_6, or_5_out, and_5_out);
  xnor xnor_4 (out_7, or_6_out, in_1);
  xnor xnor_5 (out_8, or_6_out, or_4_out);
endmodule

module TN3 (
  input  A,
  input  B,
  input  C,
  input  D,
  output F
);

  wire and_1_out, and_2_out, and_3_out, and_4_out, and_5_out, and_6_out, not_1_out, not_2_out, not_3_out,
       not_4_out;

  not not_1 (not_1_out, A);
  not not_2 (not_2_out, B);
  not not_3 (not_3_out, C);
  not not_4 (not_4_out, D);
  and and_1 (and_1_out, not_1_out, not_2_out, C, not_4_out);
  and and_2 (and_2_out, not_1_out, not_2_out, C, D);
  and and_3 (and_3_out, not_1_out, B, not_3_out, D);
  or or_1 (F, and_1_out, and_2_out, and_3_out, and_4_out, and_5_out, and_6_out);
  and and_4 (and_4_out, not_1_out, B, C, D);
  and and_5 (and_5_out, A, not_2_out, C, D);
  and and_6 (and_6_out, A, B, not_3_out, D);
endmodule

module TN4 (
  input  A,
  input  B,
  input  C,
  input  D,
  output F_can,
  output EQ1,
  output EQ2
);

  wire and_1_out, and_2_out, and_3_out, and_4_out, and_5_out, and_6_out, and_7_out, and_8_out, and_9_out,
       and_10_out, F_pos_out, F_sop_out, not_1_out, not_2_out, not_3_out, not_4_out, or_2_out, or_3_out,
       or_4_out, or_5_out;

  not not_1 (not_1_out, A);
  not not_2 (not_2_out, B);
  not not_3 (not_3_out, C);
  not not_4 (not_4_out, D);
  and and_1 (and_1_out, not_1_out, not_2_out, C, not_4_out);
  and and_2 (and_2_out, not_1_out, not_2_out, C, D);
  and and_3 (and_3_out, not_1_out, B, C, D);
  and and_4 (and_4_out, not_1_out, B, not_3_out, D);
  or or_1 (F_can, and_1_out, and_2_out, and_4_out, and_3_out, and_5_out, and_6_out);
  and and_5 (and_5_out, A, not_2_out, C, D);
  and and_6 (and_6_out, A, B, not_3_out, D);
  and and_7 (and_7_out, not_1_out, not_2_out, C);
  and and_8 (and_8_out, not_2_out, C, D);
  or F_sop (F_sop_out, and_7_out, and_8_out, and_9_out, and_10_out);
  xnor xnor_1 (EQ1, F_can, F_sop_out);
  and and_9 (and_9_out, not_1_out, B, D);
  and and_10 (and_10_out, B, not_3_out, D);
  or or_2 (or_2_out, B, C);
  or or_3 (or_3_out, not_1_out, D);
  or or_4 (or_4_out, not_2_out, D);
  and F_pos (F_pos_out, or_3_out, or_2_out, or_4_out, or_5_out);
  xnor xnor_2 (EQ2, F_can, F_pos_out);
  or or_5 (or_5_out, not_1_out, not_2_out, not_3_out);
endmodule

module TN5 (
  input  A,
  input  B,
  input  C,
  output F
);

  wire xor_1_out;

  xor xor_1 (xor_1_out, B, A);
  xor xor_2 (F, C, xor_1_out);
endmodule
