// Logisim project IT012_Lab02_25522054.circ as structural Verilog: 10 circuits, main circuit Warmup
module Warmup (
  input  [7:0] A,
  input  [7:0] B,
  output [7:0] out_3
);

  Adder adder_1 (.a(A), .b(B), .out(out_3));  // open: cin, cout
  // Probe on out_3
endmodule

module main (
  input  [7:0] in_1,
  output [7:0] out_2
);

  Warmup warmup_1 (.A(in_1), .out_3(out_2));  // open: B
endmodule

module FA (
  input  A,
  input  B,
  input  Cin,
  output S,
  output Cout
);

  wire and_1_out, and_2_out, xor_1_out;

  xor xor_1 (xor_1_out, A, B);
  and and_1 (and_1_out, A, B);
  and and_2 (and_2_out, Cin, xor_1_out);
  xor xor_2 (S, xor_1_out, Cin);
  or or_1 (Cout, and_1_out, and_2_out);
endmodule

module ADDSUB4 (
  input  [3:0] A,
  input  [3:0] B,
  input  SUB,
  output [3:0] S,
  output C,
  output Z,
  output N,
  output V
);

  wire fa_1_cout, fa_2_cout, fa_4_cout, xor_1_out, xor_2_out, xor_3_out, xor_4_out, xor_5_out, xor_6_out;

  xor xor_1 (xor_1_out, SUB, B[0]);
  xor xor_2 (xor_2_out, SUB, B[1]);
  xor xor_3 (xor_3_out, SUB, B[2]);
  xor xor_4 (xor_4_out, SUB, B[3]);
  FA fa_1 (.A(A[0]), .B(xor_1_out), .Cin(SUB), .S(S[0]), .Cout(fa_1_cout));
  FA fa_2 (.A(A[1]), .B(xor_2_out), .Cin(fa_1_cout), .S(S[1]), .Cout(fa_2_cout));
  // Probe on fa_1_cout
  xor xor_5 (xor_5_out, xor_4_out, N);
  and and_1 (V, xor_5_out, xor_6_out);
  FA fa_3 (.A(A[3]), .B(xor_4_out), .Cin(fa_4_cout), .S(N), .Cout(C));
  FA fa_4 (.A(A[2]), .B(xor_3_out), .Cin(fa_2_cout), .S(S[2]), .Cout(fa_4_cout));
  // Probe on fa_4_cout
  // Probe on fa_2_cout
  xor xor_6 (xor_6_out, N, A[3]);
  nor nor_1 (Z, S[0], S[1], S[2], N);

  assign S[3] = N;
endmodule

module ALU8 (
  input  [7:0] A,
  input  [7:0] B,
  input  [2:0] OP,
  output LT,
  output [7:0] R,
  output Z
);

  wire [7:0] adder_1_out, adder_2_out, and_1_out, multiplexer_1_out, multiplexer_2_out, not_1_out, or_1_out,
       subtractor_1_out, subtractor_2_out, xor_1_out;

  Adder adder_1 (.a(A), .b(B), .out(adder_1_out));  // open: cin, cout
  Adder adder_2 (.a(A), .b(8'h1), .out(adder_2_out));  // open: cin, cout
  Subtractor subtractor_1 (.a(A), .b(B), .out(subtractor_1_out));  // open: bin, bout
  Subtractor subtractor_2 (.a(A), .b(8'h1), .out(subtractor_2_out));  // open: bin, bout
  assign and_1_out = A & B;  // AND_Gate and_1, 8 bits wide
  assign or_1_out = A | B;  // OR_Gate or_1, 8 bits wide
  assign not_1_out = ~A;  // NOT_Gate not_1, 8 bits wide
  assign xor_1_out = A ^ B;  // XOR_Gate xor_1, 8 bits wide
  LT lt_1 (.A7(R[7]), .B7(B[7]), .R7(A[7]), .LT(LT));
  Multiplexer #(.select(2), .width(8)) multiplexer_1 (
    .in0(adder_1_out), .in1(adder_2_out), .in2(subtractor_1_out), .in3(subtractor_2_out),
    .out(multiplexer_1_out), .sel(OP[1:0]));  // open: en
  Multiplexer #(.select(2), .width(8)) multiplexer_2 (
    .in0(and_1_out), .in1(or_1_out), .in2(not_1_out), .in3(xor_1_out), .out(multiplexer_2_out), .sel(OP[1:0]));  // open: en
  Multiplexer #(.width(8)) multiplexer_3 (
    .in0(multiplexer_1_out), .in1(multiplexer_2_out), .out(R), .sel(OP[2]));  // open: en
  nor nor_1 (Z, R[0], R[1], R[2], R[3], R[4], R[5], R[6], R[7]);
endmodule

module LT (
  input  A7,
  input  B7,
  input  R7,
  output LT
);

  wire and_1_out, and_2_out, and_3_out, not_1_out;

  not not_1 (not_1_out, B7);
  and and_1 (and_1_out, A7, not_1_out);
  and and_2 (and_2_out, A7, R7);
  and and_3 (and_3_out, not_1_out, R7);
  or or_1 (LT, and_1_out, and_2_out, and_3_out);
endmodule

module TN3 (
  input  CLK,
  input  D,
  output _2_latch,
  output _2_flip_flop,
  output Q1,
  output Q2
);

  wire d_ff_1_q, dlatch_1_q;

  DLATCH dlatch_1 (.D(D), .E(CLK), .Q(dlatch_1_q));
  DLATCH dlatch_2 (.D(dlatch_1_q), .E(CLK), .Q(_2_latch));
  D_Flip_Flop d_ff_1 (.clk(CLK), .D(D), .Q(d_ff_1_q));  // open: Qn, preset, en, reset
  D_Flip_Flop d_ff_2 (.clk(CLK), .D(d_ff_1_q), .Q(_2_flip_flop));  // open: Qn, preset, en, reset
  DLATCH dlatch_3 (.D(D), .E(CLK), .Q(Q1));
  D_Flip_Flop d_ff_3 (.clk(CLK), .D(D), .Q(Q2));  // open: Qn, preset, en, reset
endmodule

module DLATCH (
  input  D,
  input  E,
  output Q
);

  Multiplexer multiplexer_1 (.in0(Q), .in1(D), .out(Q), .sel(E));  // open: en
endmodule

module REGFILE (
  input  WE,
  input  [7:0] DIN,
  input  [1:0] RA,
  input  [1:0] RD,
  input  [1:0] RB,
  input  CLK,
  output [7:0] QA,
  output [7:0] R0,
  output [7:0] R1,
  output [7:0] R2,
  output [7:0] QB,
  output [7:0] R3
);

  wire and_1_out, and_2_out, and_3_out, and_4_out, decoder_1_out0, decoder_1_out1, decoder_1_out2,
       decoder_1_out3;

  Decoder #(.select(2)) decoder_1 (
    .out0(decoder_1_out0), .out1(decoder_1_out1), .out2(decoder_1_out2), .out3(decoder_1_out3), .sel(RD));  // open: en
  and and_1 (and_1_out, decoder_1_out0, WE);
  and and_2 (and_2_out, decoder_1_out1, WE);
  and and_3 (and_3_out, decoder_1_out2, WE);
  and and_4 (and_4_out, decoder_1_out3, WE);
  Register u_R0 (.D(DIN), .en(and_1_out), .Q(R0), .clk(CLK));  // open: clr
  Register u_R1 (.D(DIN), .en(and_2_out), .Q(R1), .clk(CLK));  // open: clr
  Register u_R2 (.D(DIN), .en(and_3_out), .Q(R2), .clk(CLK));  // open: clr
  Register u_R3 (.D(DIN), .en(and_4_out), .Q(R3), .clk(CLK));  // open: clr
  Multiplexer #(.select(2), .width(8)) multiplexer_1 (
    .in0(R0), .in1(R1), .in2(R2), .in3(R3), .out(QA), .sel(RA));  // open: en
  Multiplexer #(.select(2), .width(8)) multiplexer_2 (
    .in0(R0), .in1(R1), .in2(R2), .in3(R3), .out(QB), .sel(RB));  // open: en
endmodule

module DATAPATH (
  input  [1:0] RB,
  input  [2:0] OP,
  input  [1:0] RA,
  input  [7:0] IMM,
  input  CLK,
  input  [1:0] RD,
  input  SRC,
  input  WE,
  output [7:0] R0,
  output [7:0] R1,
  output [7:0] R2,
  output [7:0] R,
  output Z,
  output [7:0] R3
);

  wire alu8_1_p4;
  wire [7:0] alu8_1_p1, alu8_1_p2, multiplexer_1_out;

  // ALU8 alu8_1: pin names not known; wires that end beside it: alu8_1_p1, alu8_1_p2, OP, alu8_1_p4, Z, R
  Multiplexer #(.width(8)) multiplexer_1 (.in0(R), .in1(IMM), .out(multiplexer_1_out), .sel(SRC));  // open: en
  REGFILE regfile_1 (
    .WE(WE), .DIN(multiplexer_1_out), .RD(RD), .CLK(CLK), .R3(R3), .RA(RA), .RB(RB), .QA(alu8_1_p1), .R0(R0),
    .R1(R1), .R2(R2), .QB(alu8_1_p2));
endmodule
